// Logisim project 4BIT-MULTIPLIER-AHHHHH.circ as structural Verilog: 1 circuit, main circuit main
module main (
  input  B3,
  input  B2,
  input  B1,
  input  B0,
  input  A3,
  input  A2,
  input  A1,
  input  A0,
  output P7,
  output P6,
  output P5,
  output P4,
  output P3,
  output P2,
  output P1,
  output P0
);

  wire A0B1_out, A0B2_out, A0B3_out, A1B0_out, A1B1_out, A1B2_out, A1B3_out, A2B0_out, A2B1_out, A2B2_out,
       A2B3_out, A3B0_out, A3B1_out, A3B2_out, A3B3_out, adder_1_cout, adder_1_out, adder_3_cout,
       adder_3_out, adder_4_cout, adder_4_out, adder_5_cout, adder_5_out, adder_6_cout, adder_7_cout,
       adder_7_out, adder_8_cout, C0_out, C3_out, C4_out, C8_out, S4_out;

  and A3B2 (A3B2_out, A3, B2);
  and A3B3 (A3B3_out, A3, B3);
  and A3B1 (A3B1_out, A3, B1);
  xor S4 (S4_out, A3B1_out, adder_4_cout);
  and C3 (C3_out, A3B1_out, adder_4_cout);
  and A2B2 (A2B2_out, A2, B2);
  Adder #(.width(1)) adder_1 (.a(C3_out), .b(A3B2_out), .out(adder_1_out), .cin(adder_3_cout), .cout(adder_1_cout));
  Adder #(.width(1)) adder_2 (.a(adder_1_cout), .b(A3B3_out), .out(P6), .cin(adder_6_cout), .cout(P7));
  and A3B0 (A3B0_out, B0, A3);
  and A2B1 (A2B1_out, A2, B1);
  and A1B2 (A1B2_out, A1, B2);
  Adder #(.width(1)) adder_3 (.a(A2B2_out), .b(S4_out), .out(adder_3_out), .cin(adder_5_cout), .cout(adder_3_cout));
  and A1B1 (A1B1_out, B1, A1);
  Adder #(.width(1)) adder_4 (.a(A3B0_out), .b(A2B1_out), .out(adder_4_out), .cin(adder_7_cout), .cout(adder_4_cout));
  and A0B2 (A0B2_out, A0, B2);
  and C4 (C4_out, A0B2_out, adder_7_out);
  Adder #(.width(1)) adder_5 (.a(adder_4_out), .b(A1B2_out), .out(adder_5_out), .cin(C4_out), .cout(adder_5_cout));
  Adder #(.width(1)) adder_6 (.a(A2B3_out), .b(adder_1_out), .out(P5), .cin(adder_8_cout), .cout(adder_6_cout));
  and A2B0 (A2B0_out, B0, A2);
  and A0B1 (A0B1_out, B1, A0);
  Adder #(.width(1)) adder_7 (.a(A2B0_out), .b(A1B1_out), .out(adder_7_out), .cin(C0_out), .cout(adder_7_cout));
  and C0 (C0_out, A0B1_out, A1B0_out);
  xor S5 (P2, A0B2_out, adder_7_out);
  and A1B3 (A1B3_out, A1, B3);
  and A2B3 (A2B3_out, A2, B3);
  Adder #(.width(1)) adder_8 (.a(A1B3_out), .b(adder_3_out), .out(P4), .cin(C8_out), .cout(adder_8_cout));
  and C8 (C8_out, A0B3_out, adder_5_out);
  and A1B0 (A1B0_out, B0, A1);
  xor S1 (P1, A0B1_out, A1B0_out);
  and A0B3 (A0B3_out, A0, B3);
  xor S9 (P3, A0B3_out, adder_5_out);
  and A0B0 (P0, B0, A0);

  // Notes on the sheet:
  //   C7
  //   S8
  //   C6
  //   S12
  //   C11
  //   C2
  //   S7
  //   C10
  //   S3
  //   C1
  //   S6
  //   C5
  //   S11
  //   C9
  //   S2
  //   S10
endmodule
