// Logisim project part2_final_project.circ as structural Verilog: 5 circuits, main circuit main
module main (
  input  [2:0] Op_Code,
  input  [7:0] X,
  input  [7:0] Y,
  output [7:0] Result,
  output EQ,
  output SF,
  output ZF,
  output OF,
  output CF
);

  ALU alu_1 (.X_Input(X), .Y_Input(Y), .OP_Code(Op_Code), .EQ(EQ), .SF(SF), .ZF(ZF), .OF(OF), .CF(CF), .Result(Result));
endmodule

module AND_8 (
  input  [7:0] A,
  input  [7:0] B,
  output [7:0] A_B
);

  and and_1 (A_B[0], B[0], A[0]);
  and and_2 (A_B[1], B[1], A[1]);
  and and_3 (A_B[2], B[2], A[2]);
  and and_4 (A_B[3], B[3], A[3]);
  and and_5 (A_B[4], B[4], A[4]);
  and and_6 (A_B[5], B[5], A[5]);
  and and_7 (A_B[6], B[6], A[6]);
  and and_8 (A_B[7], B[7], A[7]);
endmodule

module OR_8 (
  input  [7:0] A,
  input  [7:0] B,
  output [7:0] A_B
);

  or or_1 (A_B[0], B[0], A[0]);
  or or_2 (A_B[1], B[1], A[1]);
  or or_3 (A_B[2], B[2], A[2]);
  or or_4 (A_B[3], B[3], A[3]);
  or or_5 (A_B[4], B[4], A[4]);
  or or_6 (A_B[5], B[5], A[5]);
  or or_7 (A_B[6], B[6], A[6]);
  or or_8 (A_B[7], B[7], A[7]);
endmodule

module ALU (
  input  [2:0] OP_Code,
  input  [7:0] X_Input,
  input  [7:0] Y_Input,
  output [7:0] Result,
  output ZF,
  output CF,
  output EQ,
  output OF,
  output SF
);

  wire adder_1_cout, adder_2_cout, and_1_out, and_2_out, and_3_out, and_4_out, and_5_out, and_6_out,
       comparator_3_eq, comparator_4_eq, not_2_out, not_3_out, xor_1_1_x, xor_1_2_x, xor_1_3_x, xor_1_4_x;
  wire [0:0] comparator_1_lt;
  wire [7:0] adder_1_out, adder_2_out, not_1_out, shifter_1_out, shifter_2_out, shifter_3_out, X_AND_Y_a_b,
       X_OR_Y_a_b;

  OR_8 X_OR_Y (.A(Y_Input), .B(X_Input), .A_B(X_OR_Y_a_b));
  AND_8 X_AND_Y (.A(Y_Input), .B(X_Input), .A_B(X_AND_Y_a_b));
  Adder adder_1 (.a(X_Input), .b(Y_Input), .out(adder_1_out), .cin(1'b0), .cout(adder_1_cout));
  Adder adder_2 (.a(X_Input), .b(not_1_out), .out(adder_2_out), .cin(1'b1), .cout(adder_2_cout));
  assign not_1_out = ~Y_Input;  // NOT_Gate not_1, 8 bits wide
  Comparator #(.mode("unsigned")) comparator_1 (
    .a(X_Input), .b(Y_Input), .eq(EQ), .lt(comparator_1_lt[0]));  // open: gt
  Shifter shifter_1 (.in(X_Input), .\dist (Y_Input[2:0]), .out(shifter_1_out));
  Shifter #(.shift("lr")) shifter_2 (.in(X_Input), .\dist (Y_Input[2:0]), .out(shifter_2_out));
  Shifter #(.shift("ar")) shifter_3 (.in(X_Input), .\dist (Y_Input[2:0]), .out(shifter_3_out));
  Multiplexer #(.select(3), .width(8), .enable("false")) multiplexer_1 (
    .in0(X_OR_Y_a_b), .in1(X_AND_Y_a_b), .in2(adder_1_out), .in3(adder_2_out), .in4(shifter_1_out),
    .in5(shifter_2_out), .in6(shifter_3_out), .in7({{7{1'b0}}, comparator_1_lt[0]}), .out(Result),
    .sel(OP_Code));
  Comparator #(.mode("unsigned")) comparator_2 (.a(Result), .b({8{1'b0}}), .eq(ZF));  // open: gt, lt
  XOR_1 xor_1_1 (.A(X_Input[7]), .B(Y_Input[7]), .X(xor_1_1_x));
  not not_2 (not_2_out, xor_1_1_x);
  XOR_1 xor_1_2 (.A(X_Input[7]), .B(Result[7]), .X(xor_1_2_x));
  XOR_1 xor_1_3 (.A(X_Input[7]), .B(Y_Input[7]), .X(xor_1_3_x));
  XOR_1 xor_1_4 (.A(X_Input[7]), .B(Result[7]), .X(xor_1_4_x));
  and and_1 (and_1_out, not_2_out, xor_1_2_x);
  and and_2 (and_2_out, xor_1_3_x, xor_1_4_x);
  Comparator #(.width(3), .mode("unsigned")) comparator_3 (
    .a(OP_Code), .b(3'b010), .eq(comparator_3_eq));  // open: gt, lt
  Comparator #(.width(3)) comparator_4 (.a(OP_Code), .b(3'b011), .eq(comparator_4_eq));  // open: gt, lt
  not not_3 (not_3_out, adder_2_cout);
  and and_3 (and_3_out, comparator_3_eq, and_1_out);
  and and_4 (and_4_out, comparator_4_eq, and_2_out);
  and and_5 (and_5_out, comparator_3_eq, adder_1_cout);
  and and_6 (and_6_out, comparator_4_eq, not_3_out);
  or or_1 (CF, and_5_out, and_6_out);
  or or_2 (OF, and_3_out, and_4_out);

  assign SF = Result[7];

  // Notes on the sheet:
  //   X + Y
  //   X - Y
  //   Equal Comparison
  //   Sum
  //   Carry out of addition
  //   Difference
  //   Borrow out of subtraction
  //   Get 3 LSBs from Y
  //   Create 8bit number 1
  //   X OR Y 000
  //   X AND Y 001
  //   Logical Shift Right 101
  //   Arithmetic Shift Right 110
  //   X + Y 010
  //   X - Y 011
  //   Shift Left 100
  //   X <  Y 111
  //   X MSB
  //   Y MSB
  //   Zero Comparison
  //   Result MSB
  //   Carry out of addition
  //   Borrow out of subtraction
  //   X and Y have same MSB (NXOR)
  //   X and Y have different MSB (XOR)
  //   MSB of Result
  //   Check if opcode is 3 (subtraction)
  //   X and Result have different MSB (XOR)
  //   X and Result have different MSB (XOR)
  //   Check if opcode is 2 (addition)
  //   Carry Flag Addition
  //   Carry Flag Subtraction
  //   Signed Overflow Addition
  //   Signed Overflow Subtraction
endmodule

module XOR_1 (
  input  A,
  input  B,
  output X
);

  wire and_1_out, and_2_out, not_1_out, not_2_out;

  not not_1 (not_1_out, B);
  not not_2 (not_2_out, A);
  and and_1 (and_1_out, A, not_1_out);
  and and_2 (and_2_out, not_2_out, B);
  or or_1 (X, and_1_out, and_2_out);
endmodule
