// Logisim project 2bit-adder-beginner.circ as structural Verilog: 1 circuit, main circuit main
module main (
  input  Carry_in,
  input  A,
  input  B,
  input  A_2,
  input  B_2,
  output Sum,
  output Sum_2,
  output Carry_Out
);

  wire and_1_out, and_2_out, and_3_out, and_4_out, or_1_out, xor_1_out, xor_2_out;

  and and_1 (and_1_out, B, A);
  or or_1 (or_1_out, and_1_out, and_3_out);
  and and_2 (and_2_out, B_2, A_2);
  or or_2 (Carry_Out, and_2_out, and_4_out);
  xor xor_1 (xor_1_out, A, B);
  and and_3 (and_3_out, xor_1_out, Carry_in);
  xor xor_2 (xor_2_out, A_2, B_2);
  and and_4 (and_4_out, xor_2_out, or_1_out);
  xor xor_3 (Sum, Carry_in, xor_1_out);
  xor xor_4 (Sum_2, or_1_out, xor_2_out);
endmodule
