// Logisim project 3bit-mul.circ as structural Verilog: 1 circuit, main circuit main
module main (
  input  B2,
  input  B1,
  input  B0,
  input  A2,
  input  A1,
  input  A0,
  output P5,
  output P4,
  output P3,
  output P2,
  output P1,
  output P0
);

  wire A0B1_out, A1B0_out, A1B1_out, A2B0_out, A2B1_out, A2B2_out, adder_2_cout, adder_3_cout, adder_3_out,
       B2A0_out, B2A1_out, C0_out, C2_out, C3_out, S3_out;

  and A2B2 (A2B2_out, B2, A2);
  Adder #(.width(1)) adder_1 (.a(C2_out), .b(A2B2_out), .out(P4), .cin(adder_2_cout), .cout(P5));
  and A2B1 (A2B1_out, B1, A2);
  and C2 (C2_out, A2B1_out, adder_3_cout);
  xor S3 (S3_out, A2B1_out, adder_3_cout);
  and B2A1 (B2A1_out, B2, A1);
  Adder #(.width(1)) adder_2 (.a(B2A1_out), .b(S3_out), .out(P3), .cin(C3_out), .cout(adder_2_cout));
  and A2B0 (A2B0_out, B0, A2);
  and B2A0 (B2A0_out, B2, A0);
  and C3 (C3_out, B2A0_out, adder_3_out);
  xor S4 (P2, B2A0_out, adder_3_out);
  and A1B0 (A1B0_out, B0, A1);
  and A1B1 (A1B1_out, B1, A1);
  Adder #(.width(1)) adder_3 (.a(A1B1_out), .b(A2B0_out), .out(adder_3_out), .cin(C0_out), .cout(adder_3_cout));
  and C0 (C0_out, A1B0_out, A0B1_out);
  and A0B0 (P0, B0, A0);
  and A0B1 (A0B1_out, B1, A0);
  xor S1 (P1, A1B0_out, A0B1_out);

  // Notes on the sheet:
  //   S6
  //   C5
  //   S5
  //   C4
  //   C1
  //   S2
endmodule
