// Logisim project 8x1-8bit-mux.circ as structural Verilog: 1 circuit, main circuit main
module main (
  input  A,
  input  B,
  input  C,
  input  [7:0] i0,
  input  [7:0] i1,
  input  [7:0] i2,
  input  [7:0] i3,
  input  [7:0] i4,
  input  [7:0] i5,
  input  [7:0] i6,
  input  [7:0] i7,
  output [7:0] out_12
);

  wire [7:0] and_1_out, and_2_out, and_3_out, and_4_out, and_5_out, and_6_out, and_7_out, and_8_out,
       not_1_out, not_2_out, not_3_out;

  assign not_1_out = ~{8{A}};  // NOT_Gate not_1, 8 bits wide
  assign not_2_out = ~{8{C}};  // NOT_Gate not_2, 8 bits wide
  assign not_3_out = ~{8{B}};  // NOT_Gate not_3, 8 bits wide
  assign and_1_out = i0 & not_1_out & not_3_out & not_2_out;  // AND_Gate and_1, 8 bits wide
  assign and_2_out = i1 & not_1_out & not_3_out & {8{C}};  // AND_Gate and_2, 8 bits wide
  assign and_3_out = i2 & not_1_out & {8{B}} & not_2_out;  // AND_Gate and_3, 8 bits wide
  assign and_4_out = i3 & not_1_out & {8{B}} & {8{C}};  // AND_Gate and_4, 8 bits wide
  assign and_5_out = i4 & {8{A}} & not_3_out & not_2_out;  // AND_Gate and_5, 8 bits wide
  assign and_6_out = i5 & {8{A}} & not_3_out & {8{C}};  // AND_Gate and_6, 8 bits wide
  assign and_7_out = i6 & {8{A}} & {8{B}} & not_2_out;  // AND_Gate and_7, 8 bits wide
  assign and_8_out = i7 & {8{A}} & {8{B}} & {8{C}};  // AND_Gate and_8, 8 bits wide
  assign out_12 = and_1_out | and_2_out | and_3_out | and_4_out | and_5_out | and_6_out | and_7_out | and_8_out;  // OR_Gate or_1, 8 bits wide
endmodule
